// Logisim project Physics_CPU.circ as structural Verilog: 7 circuits, main circuit main
module main (
  input  in_1
);

  wire aluRegOut, and_1_out, aRegLoad, aRegOut, bRegLoad, bRegOut, clock_1_out, counterOut, displayLoad,
       increment, instructionRegLoad, instructionRegOut, loadAddress, loadCounter, memoryOut, not_1_out, sub,
       writeMemory;
  wire [2:0] flags;
  wire [7:0] A_Register_dataout, B_Register_dataout, eightbitcounter_1_counterout,
       Instruction_Register_dataout;
  wire [15:0] controlmodule_1_controlbits;

  Clock clock_1 (.out(clock_1_out));
  buf and_1 (and_1_out, clock_1_out);  // AND_Gate
  not not_1 (not_1_out, and_1_out);
  EightBitCounter eightbitcounter_1 (
    .enableOutput(counterOut), .load(loadCounter), .addressIn(eightbitcounter_1_counterout),
    .increment(increment), .clock(and_1_out), .reset(in_1), .counterOut(eightbitcounter_1_counterout));
  Memory memory_1 (
    .loadAddress(loadAddress), .reset(in_1), .address(eightbitcounter_1_counterout),
    .dataIn(eightbitcounter_1_counterout), .write(writeMemory), .clock(and_1_out), .enableOutput(memoryOut),
    .dataOut(eightbitcounter_1_counterout));
  EightBitReg Instruction_Register (
    .clock(and_1_out), .load(instructionRegLoad), .enableOutput(instructionRegOut), .reset(in_1),
    .dataIn(eightbitcounter_1_counterout), .dataOut(Instruction_Register_dataout));  // open: bufferedOut
  ControlModule controlmodule_1 (
    .instruction(Instruction_Register_dataout), .flags(flags), .clock(not_1_out),
    .controlBits({controlmodule_1_controlbits[15], writeMemory, memoryOut, instructionRegLoad, loadAddress, aRegLoad, aRegOut, bRegLoad, displayLoad, increment, loadCounter, counterOut, aluRegOut, sub, controlmodule_1_controlbits[1:0]}));
  Display display_1 (.reset(in_1), .clock(and_1_out), .displayLoad(displayLoad), .dataIn(eightbitcounter_1_counterout));
  EightBitReg A_Register (
    .clock(and_1_out), .load(aRegLoad), .enableOutput(aRegOut), .reset(in_1),
    .dataIn(eightbitcounter_1_counterout), .bufferedOut(eightbitcounter_1_counterout),
    .dataOut(A_Register_dataout));
  ALU alu_1 (
    .A(A_Register_dataout), .B(B_Register_dataout), .sub(sub), .enableOutput(aluRegOut), .clock(and_1_out),
    .reset(in_1), .calcOut(eightbitcounter_1_counterout), .flags(flags));
  EightBitReg B_Register (
    .clock(and_1_out), .load(bRegLoad), .enableOutput(bRegOut), .reset(in_1),
    .dataIn(eightbitcounter_1_counterout), .bufferedOut(eightbitcounter_1_counterout),
    .dataOut(B_Register_dataout));

  // Other names for the same wires on the sheet: reset = in_1
endmodule

module EightBitReg (
  input  clock,
  input  load,
  input  enableOutput,
  input  reset,
  input  [7:0] dataIn,
  output [7:0] bufferedOut,
  output [7:0] dataOut
);

  Register register_1 (.D(dataIn), .en(load), .clk(clock), .Q(dataOut), .clr(reset));
  assign bufferedOut = enableOutput ? dataOut : 8'bz;  // Controlled_Buffer controlled_buffer_1
endmodule

module ALU (
  input  [7:0] A,
  input  [7:0] B,
  input  sub,
  input  enableOutput,
  input  clock,
  input  reset,
  output [7:0] calcOut,
  output [2:0] flags
);

  wire and_1_out, and_2_out, nor_1_out, nor_2_out, nor_3_out, nor_4_out;
  wire [1:0] and_3_out;
  wire [7:0] adder_1_out, xor_1_out;

  assign xor_1_out = B ^ {8{sub}};  // XOR_Gate xor_1, 8 bits wide
  Adder adder_1 (.a(A), .b(xor_1_out), .out(adder_1_out), .cin(sub), .cout(and_3_out[1]));
  assign calcOut = enableOutput ? adder_1_out : 8'bz;  // Controlled_Buffer controlled_buffer_1
  nor nor_1 (nor_1_out, adder_1_out[0], adder_1_out[1]);
  nor nor_2 (nor_2_out, adder_1_out[2], adder_1_out[3]);
  nor nor_3 (nor_3_out, adder_1_out[4], adder_1_out[5]);
  nor nor_4 (nor_4_out, adder_1_out[6], adder_1_out[7]);
  and and_1 (and_1_out, nor_1_out, nor_2_out);
  and and_2 (and_2_out, nor_3_out, nor_4_out);
  and and_3 (and_3_out[0], and_1_out, and_2_out);
  Register #(.width(3)) register_1 (.D({1'b0, and_3_out}), .en(1'b1), .clk(clock), .Q(flags), .clr(reset));
endmodule

module EightBitCounter (
  input  enableOutput,
  input  load,
  input  [7:0] addressIn,
  input  increment,
  input  clock,
  input  reset,
  output [7:0] counterOut
);

  wire and_1_out, not_1_out, or_1_out;
  wire [7:0] adder_1_out, bit_extender_1_out, multiplexer_1_out, register_1_q;

  Adder adder_1 (.a(register_1_q), .b(bit_extender_1_out), .out(adder_1_out));  // open: cin, cout
  assign bit_extender_1_out = {{7{1'b0}}, increment};  // Bit_Extender bit_extender_1
  and and_1 (and_1_out, increment, not_1_out);
  not not_1 (not_1_out, load);
  Multiplexer #(.width(8)) multiplexer_1 (.in0(addressIn), .in1(adder_1_out), .out(multiplexer_1_out), .sel(and_1_out));
  Register register_1 (.D(multiplexer_1_out), .en(or_1_out), .clk(clock), .Q(register_1_q), .clr(reset));
  or or_1 (or_1_out, load, increment);
  assign counterOut = enableOutput ? register_1_q : 8'bz;  // Controlled_Buffer controlled_buffer_1
endmodule

module Memory (
  input  loadAddress,
  input  reset,
  input  [7:0] address,
  input  [7:0] dataIn,
  input  write,
  input  clock,
  input  enableOutput,
  output [7:0] dataOut
);

  wire [7:0] ram_1_dout, register_1_q;

  Register register_1 (.D(address), .en(loadAddress), .clk(clock), .Q(register_1_q), .clr(reset));
  RAM #(.enables("line")) ram_1 (.addr(register_1_q), .we(write), .clk(clock), .din(dataIn), .dout(ram_1_dout));
  assign dataOut = enableOutput ? ram_1_dout : 8'bz;  // Controlled_Buffer controlled_buffer_1
endmodule

module ControlModule (
  input  [7:0] instruction,
  input  [2:0] flags,
  input  clock,
  output [15:0] controlBits
);

  wire [7:0] eightbitcounter_1_counterout;

  EightBitCounter eightbitcounter_1 (
    .enableOutput(1'b1), .increment(1'b1), .clock(clock), .reset(controlBits[1]),
    .counterOut(eightbitcounter_1_counterout));  // open: load, addressIn
  // Probe on {eightbitcounter_1_counterout[3:0], flags, instruction}
  ROM #(.addrWidth(15)) rom_1 (.addr({eightbitcounter_1_counterout[3:0], flags, instruction}), .data(controlBits[7:0]));
  ROM #(.addrWidth(15)) rom_2 (
    .addr({eightbitcounter_1_counterout[3:0], flags, instruction}), .data(controlBits[15:8]));
  // Probe on controlBits

  // Notes on the sheet:
  //   contents of rom_1 (hex, n*v repeats v):
  //   2048*10 2048*40 2 8*10 80 0 246*2 8*10 80 0 246*2 8*10 80 0 246*2 8*10 80 0 246*2 8*10 80 0 246*2
  //   8*10 80 0 246*2 8*10 80 0 246*2 8*10 80 0 245*2 0 7*40 20 2 2 246*0 7*40 20 2 2 246*0 7*40 20 2 2
  //   246*0 7*40 20 2 2 246*0 7*40 20 2 2 246*0 7*40 20 2 2 246*0 7*40 20 2 2 246*0 7*40 20 2 2 248*0 8 0
  //   8 0 2 2 250*0 8 0 8 0 2 2 250*0 8 0 8 0 2 2 250*0 8 0 8 0 2 2 250*0 8 0 8 0 2 2 250*0 8 0 8 0 2 2
  //   250*0 8 0 8 0 2 2 250*0 8 0 8 0 2 2 248*0 2 8 2 c 2 2 250*0 2 8 2 c 2 2 250*0 2 8 2 c 2 2 250*0 2 8
  //   2 c 2 2 250*0 2 8 2 c 2 2 250*0 2 8 2 c 2 2 250*0 2 8 2 c 2 2 250*0 2 8 2 c 2 2 251*0 2 0 2 253*0 2
  //   0 2 253*0 2 0 2 253*0 2 0 2 253*0 2 0 2 253*0 2 0 2 253*0 2 0 2 253*0 2 0 2
  //   contents of rom_2 (hex, n*v repeats v):
  //   2048*8 2048*30 0 8*8 2 80 246*0 8*8 2 80 246*0 8*8 2 80 246*0 8*8 2 80 246*0 8*8 2 80 246*0 8*8 2 80
  //   246*0 8*8 2 80 246*0 8*8 2 80 246*0 28 28 21 28 21 28 24 20 248*0 28 28 21 28 21 28 24 20 248*0 28
  //   28 21 28 21 28 24 20 248*0 28 28 21 28 21 28 24 20 248*0 28 28 21 28 21 28 24 20 248*0 28 28 21 28
  //   21 28 24 20 248*0 28 28 21 28 21 28 24 20 248*0 28 28 21 28 21 28 24 20 248*0 24 21 4 21 4 42 250*0
  //   24 21 4 21 4 42 250*0 24 21 4 21 4 42 250*0 24 21 4 21 4 42 250*0 24 21 4 21 4 42 250*0 24 21 4 21 4
  //   42 250*0 24 21 4 21 4 42 250*0 24 21 4 21 4 42 251*0 4 0 4 253*0 4 0 4 253*0 4 0 4 253*0 4 0 4 253*0
  //   4 0 4 253*0 4 0 4 253*0 4 0 4 253*0 4 0 4
endmodule

module Display (
  input  reset,
  input  clock,
  input  displayLoad,
  input  [7:0] dataIn
);

  wire bcd_to_7_segment_decoder_3_p1, binary_to_bcd_converter_1_p1, binary_to_bcd_converter_1_p3;
  wire [7:0] register_1_q;

  Register register_1 (.D(dataIn), .en(displayLoad), .clk(clock), .Q(register_1_q), .clr(reset));
  _7_Segment_Display u_7_segment_display_1 ();  // open: g, f, a, b, e, d, c, dp
  // BCD_to_7_Segment_decoder bcd_to_7_segment_decoder_1: pin names not known
  // Binary_to_BCD_converter binary_to_bcd_converter_1: pin names not known; wires that end beside it: binary_to_bcd_converter_1_p1, binary_to_bcd_converter_1_p1, binary_to_bcd_converter_1_p3
  _7_Segment_Display u_7_segment_display_2 ();  // open: g, f, a, b, e, d, c, dp
  // BCD_to_7_Segment_decoder bcd_to_7_segment_decoder_2: pin names not known; wires that end beside it: binary_to_bcd_converter_1_p3
  _7_Segment_Display u_7_segment_display_3 ();  // open: g, f, a, b, e, d, c, dp
  // BCD_to_7_Segment_decoder bcd_to_7_segment_decoder_3: pin names not known; wires that end beside it: bcd_to_7_segment_decoder_3_p1, bcd_to_7_segment_decoder_3_p1
endmodule
